// Logisim project Array_Multiplier.circ as structural Verilog: 2 circuits, main circuit main
module main (
  input  b3,
  input  b2,
  input  b1,
  input  b0,
  input  b3_2,
  input  b2_2,
  input  b1_2,
  input  b0_2,
  input  a0,
  input  a1,
  input  in_11,
  input  b3_3,
  input  b2_3,
  input  b1_3,
  input  b0_3,
  input  a2,
  input  b3_4,
  input  b2_4,
  input  b1_4,
  input  b0_4,
  input  a3,
  output c7,
  output c6,
  output c5,
  output c4,
  output c3,
  output c2,
  output c1,
  output c0
);

  wire and_1_out, and_2_out, and_3_out, and_4_out, and_5_out, and_6_out, and_7_out, and_8_out, and_9_out,
       and_10_out, and_11_out, and_12_out, and_13_out, and_14_out, and_15_out, n4_bit_adder_2_s1,
       n4_bit_adder_2_s2, n4_bit_adder_2_s3, n4_bit_adder_2_s4, n4_bit_adder_3_s1, n4_bit_adder_3_s2,
       n4_bit_adder_3_s3, n4_bit_adder_3_s4;

  and and_1 (and_1_out, a3, b3_4);
  and and_2 (and_2_out, a3, b2_4);
  and and_3 (and_3_out, a3, b1_4);
  and and_4 (and_4_out, a3, b0_4);
  and and_5 (and_5_out, a2, b3_3);
  and and_6 (and_6_out, a2, b2_3);
  and and_7 (and_7_out, a2, b1_3);
  and and_8 (and_8_out, a1, b3);
  and and_9 (and_9_out, a2, b0_3);
  _4_bit_Adder u_4_bit_adder_1 (
    .B0(n4_bit_adder_2_s1), .B1(n4_bit_adder_2_s2), .B2(n4_bit_adder_2_s3), .B3(n4_bit_adder_2_s4),
    .A0(and_4_out), .A1(and_3_out), .A2(and_2_out), .A3(and_1_out), .C0(c3), .S1(c4), .S2(c5), .S3(c6),
    .S4(c7));
  and and_10 (and_10_out, a1, b2);
  and and_11 (and_11_out, a1, b1);
  and and_12 (and_12_out, a1, b0);
  _4_bit_Adder u_4_bit_adder_2 (
    .B0(n4_bit_adder_3_s1), .B1(n4_bit_adder_3_s2), .B2(n4_bit_adder_3_s3), .B3(n4_bit_adder_3_s4),
    .A0(and_9_out), .A1(and_7_out), .A2(and_6_out), .A3(and_5_out), .C0(c2), .S1(n4_bit_adder_2_s1),
    .S2(n4_bit_adder_2_s2), .S3(n4_bit_adder_2_s3), .S4(n4_bit_adder_2_s4));
  _4_bit_Adder u_4_bit_adder_3 (
    .B0(and_14_out), .B1(and_15_out), .B2(and_13_out), .B3(in_11), .A0(and_12_out), .A1(and_11_out),
    .A2(and_10_out), .A3(and_8_out), .C0(c1), .S1(n4_bit_adder_3_s1), .S2(n4_bit_adder_3_s2),
    .S3(n4_bit_adder_3_s3), .S4(n4_bit_adder_3_s4));
  and and_13 (and_13_out, a0, b3_2);
  and and_14 (and_14_out, a0, b1_2);
  and and_15 (and_15_out, a0, b2_2);
  and and_16 (c0, a0, b0_2);
endmodule

module _4_bit_Adder (
  input  B0,
  input  B1,
  input  B2,
  input  B3,
  input  A0,
  input  A1,
  input  A2,
  input  A3,
  output C0,
  output S1,
  output S2,
  output S3,
  output S4
);

  wire and_1_out, and_2_out, and_3_out, and_4_out, and_5_out, and_6_out, and_7_out, or_1_out, or_2_out,
       xor_2_out, xor_3_out, xor_4_out;

  xor xor_1 (C0, A0, B0);
  and and_1 (and_1_out, A0, B0);
  xor xor_2 (xor_2_out, A1, B1);
  and and_2 (and_2_out, B1, A1);
  xor xor_3 (xor_3_out, A2, B2);
  and and_3 (and_3_out, B2, A2);
  xor xor_4 (xor_4_out, A3, B3);
  and and_4 (and_4_out, B3, A3);
  and and_5 (and_5_out, and_1_out, xor_2_out);
  xor xor_5 (S2, xor_3_out, or_1_out);
  and and_6 (and_6_out, or_1_out, xor_3_out);
  and and_7 (and_7_out, or_2_out, xor_4_out);
  xor xor_6 (S1, xor_2_out, and_1_out);
  xor xor_7 (S3, xor_4_out, or_2_out);
  or or_1 (or_1_out, and_5_out, and_2_out);
  or or_2 (or_2_out, and_6_out, and_3_out);
  or or_3 (S4, and_7_out, and_4_out);
endmodule
